// Logisim project 130_velasco_le3.circ as structural Verilog: 1 circuit, main circuit main
module main (
  input  y5,
  input  y4,
  input  y3,
  input  y2,
  input  y1,
  input  C0,
  input  Input,
  output out_8,
  output out_9,
  output out_10,
  output out_11,
  output out_12,
  output C5,
  output C4,
  output C3,
  output C2,
  output C1,
  output S4,
  output S3,
  output S2,
  output S1,
  output S5,
  output Output
);

  wire A_3_p1, A_3_p2, A_3_p3, A_p2, and_2_out, and_3_out, and_4_out, and_5_out, and_6_out, and_7_out,
       and_8_out, and_9_out, and_10_out, and_11_out, and_12_out, and_13_out, and_14_out, and_15_out,
       and_16_out, and_17_out, and_18_out, and_19_out, and_20_out, and_21_out, and_22_out, and_23_out,
       and_24_out, and_25_out, and_26_out, and_27_out, and_28_out, and_29_out, and_30_out, and_31_out,
       and_32_out, and_33_out, and_34_out, and_35_out, and_36_out, and_37_out, and_38_out, and_39_out, B_p3,
       C_3_p2, C_3_p3, C_p3, clock_1_out, clock_2_out, d_ff_2_q, d_ff_2_qn, d_ff_4_q, d_ff_4_qn, d_ff_6_q,
       d_ff_6_qn, demultiplexer_1_p1, demultiplexer_1_p2, demultiplexer_1_p3, demultiplexer_1_p4,
       demultiplexer_1_p5, demultiplexer_1_p6, demultiplexer_1_p7, demultiplexer_1_p8, demultiplexer_1_p9,
       demultiplexer_1_p10, demultiplexer_1_p11, demultiplexer_1_p12, G0_out, G1_out, G3_out, G4_out, G5_out,
       not_1_out, not_2_out, not_3_out, not_4_out, not_5_out, not_6_out, or_1_out, or_2_out, P0_out, P1_out,
       P3_out, P4_out, P5_out, undriven, undriven_2, undriven_3, undriven_4, undriven_5, undriven_6,
       xor_1_out, xor_2_out, xor_3_out, xor_4_out, xor_5_out, xor_6_out, xor_7_out, xor_8_out, xor_10_out,
       xor_12_out, xor_14_out, xor_16_out, xor_18_out;

  Clock clock_1 (.out(clock_1_out));
  and and_1 (Output, d_ff_2_qn, Input);
  Clock clock_2 (.out(clock_2_out));
  // Demultiplexer #(.select(5)) demultiplexer_1: pin names not known; wires that end beside it: demultiplexer_1_p1, demultiplexer_1_p2, demultiplexer_1_p3, demultiplexer_1_p4, demultiplexer_1_p5, demultiplexer_1_p6, demultiplexer_1_p7, demultiplexer_1_p8, demultiplexer_1_p9, demultiplexer_1_p10, demultiplexer_1_p11, demultiplexer_1_p12, demultiplexer_1_p12
  // OR_Gate A: pin names not known; wires that end beside it: demultiplexer_1_p12, A_p2
  and and_2 (and_2_out, Input, d_ff_4_qn, d_ff_2_qn);
  // OR_Gate B: pin names not known; wires that end beside it: demultiplexer_1_p12, A_p2, B_p3
  // OR_Gate C: pin names not known; wires that end beside it: A_p2, B_p3, C_p3
  xor xor_1 (xor_1_out, out_8, out_9);
  D_Flip_Flop d_ff_1 (.clk(clock_1_out), .D(S5), .Q(out_8));  // open: Qn, preset, en, reset
  and and_3 (and_3_out, Input, d_ff_6_q, d_ff_4_q, d_ff_2_qn);
  and and_4 (and_4_out, ~Input, d_ff_6_qn);  // AND_Gate
  or or_1 (or_1_out, d_ff_2_q, and_4_out, and_3_out);
  D_Flip_Flop d_ff_2 (.clk(clock_2_out), .D(and_2_out), .Q(d_ff_2_q), .Qn(d_ff_2_qn));  // open: preset, en, reset
  // OR_Gate D: pin names not known; wires that end beside it: B_p3, C_p3, demultiplexer_1_p11
  xor xor_2 (xor_2_out, xor_1_out, out_10);
  D_Flip_Flop d_ff_3 (.clk(clock_1_out), .D(xor_3_out), .Q(out_9));  // open: Qn, preset, en, reset
  xor xor_3 (xor_3_out, S5, S4);
  xor xor_4 (xor_4_out, S4, S3);
  D_Flip_Flop d_ff_4 (.clk(clock_2_out), .D(or_1_out), .Q(d_ff_4_q), .Qn(d_ff_4_qn));  // open: preset, en, reset
  xor xor_5 (xor_5_out, xor_2_out, out_12);
  xor xor_6 (xor_6_out, xor_5_out, out_11);
  D_Flip_Flop d_ff_5 (.clk(clock_1_out), .D(xor_4_out), .Q(out_10));  // open: Qn, preset, en, reset
  xor xor_7 (xor_7_out, S3, S2);
  D_Flip_Flop d_ff_6 (.clk(clock_2_out), .D(or_2_out), .Q(d_ff_6_q), .Qn(d_ff_6_qn));  // open: preset, en, reset
  or or_2 (or_2_out, and_5_out, and_6_out, and_7_out);
  D_Flip_Flop d_ff_7 (.clk(clock_1_out), .D(xor_7_out), .Q(out_12));  // open: Qn, preset, en, reset
  xor xor_8 (xor_8_out, S2, S1);
  and and_5 (and_5_out, d_ff_2_qn, d_ff_4_qn, ~Input);  // AND_Gate
  and and_6 (and_6_out, d_ff_6_q, ~Input);  // AND_Gate
  and and_7 (and_7_out, d_ff_2_q, Input);
  not not_1 (not_1_out, undriven_2);
  not not_2 (not_2_out, undriven);
  D_Flip_Flop d_ff_8 (.clk(clock_1_out), .D(xor_8_out), .Q(out_11));  // open: Qn, preset, en, reset
  not not_3 (not_3_out, undriven_3);
  // AND_Gate and_8 has open pins: out=and_8_out
  // AND_Gate and_9 has open pins: out=and_9_out
  // AND_Gate and_10 has open pins: out=and_10_out
  // AND_Gate and_11 has open pins: out=and_11_out
  // AND_Gate and_12 has open pins: out=and_12_out
  // AND_Gate and_13 has open pins: out=and_13_out
  // AND_Gate and_14 has open pins: out=and_14_out
  // AND_Gate and_15 has open pins: out=and_15_out
  // AND_Gate and_16 has open pins: out=and_16_out
  // AND_Gate and_17 has open pins: out=and_17_out
  // AND_Gate and_18 has open pins: out=and_18_out
  // AND_Gate and_19 has open pins: out=and_19_out
  // AND_Gate and_20 has open pins: out=and_20_out
  // AND_Gate and_21 has open pins: out=and_21_out
  // AND_Gate and_22 has open pins: out=and_22_out
  // AND_Gate and_23 has open pins: out=and_23_out
  // OR_Gate A_2: pin names not known; wires that end beside it: and_8_out, and_9_out, and_10_out, and_11_out
  // OR_Gate B_2: pin names not known; wires that end beside it: and_12_out, and_13_out, and_14_out, and_15_out
  // OR_Gate C_2: pin names not known; wires that end beside it: and_16_out, and_17_out, and_18_out, and_19_out
  // OR_Gate D_2: pin names not known; wires that end beside it: and_20_out, and_21_out, and_22_out, and_23_out
  not not_4 (not_4_out, undriven_4);
  and G5 (G5_out, out_8, y5);
  or or_3 (C5, G5_out, and_24_out);
  xor xor_9 (S5, out_8, xor_10_out);
  not not_5 (not_5_out, undriven_5);
  xor P5 (P5_out, out_8, y5);
  and and_24 (and_24_out, P5_out, C4);
  xor xor_10 (xor_10_out, y5, C4);
  not not_6 (not_6_out, undriven_6);
  // AND_Gate and_25 has open pins: out=and_25_out
  // AND_Gate and_26 has open pins: out=and_26_out
  // AND_Gate and_27 has open pins: out=and_27_out
  // AND_Gate and_28 has open pins: out=and_28_out
  // AND_Gate and_29 has open pins: out=and_29_out
  // AND_Gate and_30 has open pins: out=and_30_out
  // AND_Gate and_31 has open pins: out=and_31_out
  // AND_Gate and_32 has open pins: out=and_32_out
  // AND_Gate and_33 has open pins: out=and_33_out
  // AND_Gate and_34 has open pins: out=and_34_out
  // AND_Gate and_35 has open pins: out=and_35_out
  // OR_Gate A_3: pin names not known; wires that end beside it: A_3_p1, A_3_p2, A_3_p3
  and G4 (G4_out, xor_1_out, y4);
  xor P4 (P4_out, xor_1_out, y4);
  or or_4 (C4, G4_out, and_36_out);
  xor xor_11 (S4, xor_1_out, xor_12_out);
  // OR_Gate C_3: pin names not known; wires that end beside it: A_3_p3, C_3_p2, C_3_p3
  // OR_Gate B_3: pin names not known; wires that end beside it: A_3_p2, A_3_p3, C_3_p2
  and G3 (G3_out, xor_2_out, y3);
  and and_36 (and_36_out, P4_out, C3);
  xor xor_12 (xor_12_out, y4, C3);
  // OR_Gate D_3: pin names not known; wires that end beside it: C_3_p2, C_3_p3, and_35_out
  xor P3 (P3_out, xor_2_out, y3);
  or or_5 (C3, G3_out, and_37_out);
  xor xor_13 (S3, xor_2_out, xor_14_out);
  and G1 (G1_out, xor_5_out, y2);
  and and_37 (and_37_out, P3_out, C2);
  xor xor_14 (xor_14_out, y3, C2);
  xor P1 (P1_out, xor_5_out, y2);
  or or_6 (C2, G1_out, and_38_out);
  and and_38 (and_38_out, P1_out, C1);
  xor xor_15 (S2, xor_5_out, xor_16_out);
  and G0 (G0_out, xor_6_out, y1);
  xor xor_16 (xor_16_out, y2, C1);
  xor P0 (P0_out, xor_6_out, y1);
  and and_39 (and_39_out, P0_out, C0);
  or or_7 (C1, G0_out, and_39_out);
  xor xor_17 (S1, xor_6_out, xor_18_out);
  xor xor_18 (xor_18_out, y1, C0);

  // Notes on the sheet:
  //   #2
  //   #3
  //   x
  //   y
  //   z
  //   VELASCO, Gimel David F.
  //   2012-58922
  //   #1
  //   PIPO (Parallel In Parallel Out) Register
  //   x
  //   x
  //   x
  //   x
  //   A
  //   PROM
  //   x
  //   x
  //   x
  //   x
  //   x
  //   x
  //   x'y'z'
  //   x'y'z
  //   x
  //   x
  //   x'yz'
  //   x'yz
  //   x
  //   xy'z'
  //   x
  //   xy'z
  //   xyz'
  //   xyz
  //   x
  //   B
  //   Cmsc 130 LE3
  //   Gray Code to Binary
  //   C
  //   x
  //   x
  //   x
  //   x
  //   y
  //   x
  //   x
  //   x
  //   x
  //   x
  //   x
  //   x
  //   x
  //   x
  //   x
  //   x
  //   x
  //   x
  //   x
  //   x
  //   x
  //   x
  //   x
  //   x
  //   x
  //   x
  //   x
  //   x
  //   x
  //   12.3.15
  //   Binary to Gray Code
  //   z
  //   x
  //   x
  //   x
  //   x
  //   x
  //   x
  //   x
  //   x
  //   x
  //   x
  //   x
  //   x
  //   x
  //   x
  //   PAL
  //   y1 needs to be set to 1
  //   Sum
  //   x
  //   x
  //   x
  //   x
  //   x
  //   x
  //   x
  //   x
  //   x
  //   x
  //   x
  //   x
  //   x
  //   z
  //   y
  //   x
  //   x
  //   x
  //   x
  //   x
  //   x
  //   x
  //   x
  //   x
  //   x
  //   x
  //   x
  //   x
  //   x
  //   x
  //   x
  //   x
  //   x
  //   PLA
  //   x
  //   x
  //   x
  //   x
  //   x
  //   x
  //   x
  //   Increment Circuit
  //   x
  //   x
  //   x
  //   x
endmodule
