// Logisim project 130_velasco_fajardo_me10.circ as structural Verilog: 1 circuit, main circuit main
module main (
  input  x,
  input  y,
  output S
);

  wire adder_1_cout, clock_1_out, clock_2_out, d_ff_1_q, or_1_out, or_2_out, t_ff_1_q, t_ff_1_qn, t_ff_2_q,
       t_ff_2_qn;

  Clock clock_1 (.out(clock_1_out));
  Clock clock_2 (.out(clock_2_out));
  or or_1 (or_1_out, t_ff_1_q, t_ff_2_q);
  or or_2 (or_2_out, t_ff_1_qn, t_ff_2_q);
  D_Flip_Flop d_ff_1 (.clk(clock_2_out), .D(adder_1_cout), .Q(d_ff_1_q));  // open: Qn, preset, en, reset
  Adder #(.width(1)) adder_1 (.a(x), .b(y), .out(S), .cin(d_ff_1_q), .cout(adder_1_cout));
  T_Flip_Flop t_ff_1 (.clk(clock_1_out), .T(or_1_out), .Q(t_ff_1_q), .Qn(t_ff_1_qn));  // open: preset, reset, en
  T_Flip_Flop t_ff_2 (.clk(clock_1_out), .T(or_2_out), .Q(t_ff_2_q), .Qn(t_ff_2_qn));  // open: preset, reset, en

  // Notes on the sheet:
  //   A
  //   B
endmodule
