// Logisim project 130_fajardo_velasco.circ as structural Verilog: 1 circuit, main circuit main
module main (
  input  Reset,
  input  Enabler,
  input  [1:0] Selector,
  input  ShiftLeft,
  input  ShiftRight,
  input  I3,
  input  I2,
  input  I1,
  input  I0,
  output A3,
  output A2,
  output A1,
  output A0
);

  wire Clock_out, multiplexer_1_out, multiplexer_2_out, multiplexer_3_out, multiplexer_4_out;

  Clock Clock (.out(Clock_out));
  D_Flip_Flop d_ff_1 (.D(multiplexer_1_out), .clk(Clock_out), .Q(A3), .reset(Reset));  // open: Qn, preset
  Multiplexer #(.select(2)) multiplexer_1 (
    .in0(A3), .in1(ShiftRight), .in2(A2), .in3(I3), .out(multiplexer_1_out), .sel(Selector), .en(Enabler));
  D_Flip_Flop d_ff_2 (.D(multiplexer_2_out), .clk(Clock_out), .Q(A2), .reset(Reset));  // open: Qn, preset
  Multiplexer #(.select(2)) multiplexer_2 (
    .in0(A2), .in1(A3), .in2(A1), .in3(I2), .out(multiplexer_2_out), .sel(Selector), .en(Enabler));
  D_Flip_Flop d_ff_3 (.D(multiplexer_3_out), .clk(Clock_out), .Q(A1), .reset(Reset));  // open: Qn, preset
  Multiplexer #(.select(2)) multiplexer_3 (
    .in0(A1), .in1(A2), .in2(A0), .in3(I1), .out(multiplexer_3_out), .sel(Selector), .en(Enabler));
  D_Flip_Flop d_ff_4 (.D(multiplexer_4_out), .clk(Clock_out), .Q(A0), .reset(Reset));  // open: Qn, preset
  Multiplexer #(.select(2)) multiplexer_4 (
    .in0(A0), .in1(A1), .in2(ShiftLeft), .in3(I0), .out(multiplexer_4_out), .sel(Selector), .en(Enabler));
endmodule
