// Logisim project 130_lec111815.circ as structural Verilog: 1 circuit, main circuit main
module main (
  input  in_1,
  input  SIPO_Register,
  input  in3,
  input  in_4,
  input  in_5,
  input  in0,
  input  in3_2,
  input  in_8,
  input  in_9,
  input  in0_2,
  input  control,
  output out_12,
  output out3,
  output out2,
  output out1,
  output out0,
  output out3_2,
  output out2_2,
  output out1_2,
  output out0_2,
  output out_21
);

  wire and_1_out, and_2_out, and_3_out, and_4_out, and_5_out, and_6_out, clock_1_out, clock_2_out,
       clock_3_out, clock_4_out, d_ff_1_q, d_ff_4_q, d_ff_5_q, d_ff_8_q, d_ff_9_q, d_ff_12_q, load_out,
       not_1_out, or_1_out, or_2_out, or_3_out, or_4_out, shift_out;

  Clock clock_1 (.out(clock_1_out));
  Clock clock_2 (.out(clock_2_out));
  Clock clock_3 (.out(clock_3_out));
  not not_1 (not_1_out, control);
  Clock clock_4 (.out(clock_4_out));
  D_Flip_Flop d_ff_1 (.D(in_1), .clk(clock_1_out), .Q(d_ff_1_q));  // open: Qn, preset, reset
  D_Flip_Flop d_ff_2 (.D(SIPO_Register), .clk(clock_2_out), .Q(out3));  // open: Qn, preset, reset
  D_Flip_Flop d_ff_3 (.D(in3), .clk(clock_3_out), .Q(out3_2));  // open: Qn, preset, reset
  and shift (shift_out, not_1_out, in3_2);
  and load (load_out, in3_2, control);
  or or_1 (or_1_out, load_out, shift_out);
  D_Flip_Flop d_ff_4 (.D(or_1_out), .clk(clock_4_out), .Q(d_ff_4_q));  // open: Qn, preset, reset
  D_Flip_Flop d_ff_5 (.D(d_ff_1_q), .clk(clock_1_out), .Q(d_ff_5_q));  // open: Qn, preset, reset
  D_Flip_Flop d_ff_6 (.D(out3), .clk(clock_2_out), .Q(out2));  // open: Qn, preset, reset
  D_Flip_Flop d_ff_7 (.D(in_4), .clk(clock_3_out), .Q(out2_2));  // open: Qn, preset, reset
  and and_1 (and_1_out, not_1_out, d_ff_4_q);
  and and_2 (and_2_out, in_8, control);
  D_Flip_Flop d_ff_8 (.D(or_2_out), .clk(clock_4_out), .Q(d_ff_8_q));  // open: Qn, preset, reset
  or or_2 (or_2_out, and_2_out, and_1_out);
  D_Flip_Flop d_ff_9 (.D(d_ff_5_q), .clk(clock_1_out), .Q(d_ff_9_q));  // open: Qn, preset, reset
  D_Flip_Flop d_ff_10 (.D(out2), .clk(clock_2_out), .Q(out1));  // open: Qn, preset, reset
  D_Flip_Flop d_ff_11 (.D(in_5), .clk(clock_3_out), .Q(out1_2));  // open: Qn, preset, reset
  and and_3 (and_3_out, in_9, control);
  and and_4 (and_4_out, not_1_out, d_ff_8_q);
  D_Flip_Flop d_ff_12 (.D(or_3_out), .clk(clock_4_out), .Q(d_ff_12_q));  // open: Qn, preset, reset
  or or_3 (or_3_out, and_3_out, and_4_out);
  D_Flip_Flop d_ff_13 (.D(d_ff_9_q), .clk(clock_1_out), .Q(out_12));  // open: Qn, preset, reset
  D_Flip_Flop d_ff_14 (.D(out1), .clk(clock_2_out), .Q(out0));  // open: Qn, preset, reset
  D_Flip_Flop d_ff_15 (.D(in0), .clk(clock_3_out), .Q(out0_2));  // open: Qn, preset, reset
  and and_5 (and_5_out, in0_2, control);
  and and_6 (and_6_out, not_1_out, d_ff_12_q);
  D_Flip_Flop d_ff_16 (.D(or_4_out), .clk(clock_4_out), .Q(out_21));  // open: Qn, preset, reset
  or or_4 (or_4_out, and_5_out, and_6_out);

  // Notes on the sheet:
  //   SISO (Serial In - Serial Out)
  //   PIPO (Parallel In Parallel Out) Register
  //   PISO Register
  //   -Shift Mode - Serial Shift
  //   -Load Mode - Parallel write
endmodule
