// Logisim project 130_meneses_velasco_me12.circ as structural Verilog: 1 circuit, main circuit main
module main (
  input  in_1,
  input  in_2,
  input  in_3,
  input  in_4,
  input  in_5,
  input  in_6,
  input  in_7,
  input  Reset,
  output out_9,
  output out_10,
  output out_11,
  output out_12,
  output out_13,
  output out_14,
  output out_15,
  output out_16,
  output out_17,
  output out_18,
  output out_19,
  output out_20,
  output out_21
);

  wire and_1_out, and_2_out, and_3_out, and_4_out, and_5_out, and_6_out, and_7_out, and_8_out, and_9_out,
       and_10_out, and_11_out, and_12_out, and_13_out, and_14_out, and_15_out, and_16_out, and_17_out,
       and_18_out, and_19_out, and_20_out, and_21_out, and_22_out, and_23_out, and_24_out, clock_1_out,
       clock_2_out, d_ff_1_qn, d_ff_2_qn, d_ff_3_qn, d_ff_4_qn, d_ff_5_qn, d_ff_6_q, d_ff_7_qn, d_ff_8_qn,
       d_ff_9_qn, not_1_out, not_2_out, not_3_out, not_4_out, not_5_out, not_6_out, or_1_out, or_2_out,
       or_3_out, or_4_out, or_5_out, or_6_out, or_7_out, or_8_out, or_9_out, or_10_out, or_11_out, or_12_out,
       xor_1_out, xor_2_out;

  and and_1 (and_1_out, d_ff_4_qn, d_ff_3_qn, d_ff_2_qn, out_14);
  or or_1 (or_1_out, and_1_out, and_2_out);
  Clock clock_1 (.out(clock_1_out));
  and and_2 (and_2_out, out_17, out_15, out_16);
  D_Flip_Flop d_ff_1 (.D(or_1_out), .clk(and_15_out), .Q(out_14), .Qn(d_ff_1_qn), .reset(Reset));  // open: preset
  not not_1 (not_1_out, in_2);
  and and_3 (and_3_out, out_16, out_17);
  D_Flip_Flop d_ff_2 (.D(xor_1_out), .clk(and_15_out), .Q(out_15), .Qn(d_ff_2_qn), .reset(Reset));  // open: preset
  xor xor_1 (xor_1_out, and_3_out, out_15);
  and and_4 (and_4_out, in_1, not_1_out);
  not not_2 (not_2_out, not_1_out);
  not not_3 (not_3_out, in_3);
  not not_4 (not_4_out, in_4);
  not not_5 (not_5_out, in_5);
  not not_6 (not_6_out, in_6);
  and and_5 (and_5_out, d_ff_1_qn, out_17, d_ff_3_qn);
  and and_6 (and_6_out, out_16, d_ff_4_qn);
  or or_2 (or_2_out, and_5_out, and_6_out);
  D_Flip_Flop d_ff_3 (.D(or_2_out), .clk(and_15_out), .Q(out_16), .Qn(d_ff_3_qn), .reset(Reset));  // open: preset
  and and_7 (and_7_out, not_2_out, in_3);
  and and_8 (and_8_out, not_2_out, not_3_out);
  and and_9 (and_9_out, not_2_out, in_4);
  and and_10 (and_10_out, not_2_out, not_4_out);
  and and_11 (and_11_out, not_2_out, in_5);
  buf and_12 (and_12_out, not_5_out);  // AND_Gate
  and and_13 (and_13_out, not_2_out, in_6);
  and and_14 (and_14_out, not_2_out, not_6_out);
  D_Flip_Flop d_ff_4 (.D(d_ff_4_qn), .clk(and_15_out), .Q(out_17), .Qn(d_ff_4_qn), .reset(Reset));  // open: preset
  and and_15 (and_15_out, d_ff_6_q, clock_2_out);
  and and_16 (and_16_out, and_4_out, out_9);
  and and_17 (and_17_out, and_4_out, out_9, out_10);
  and and_18 (and_18_out, and_4_out, out_9, out_10, out_11);
  and and_19 (and_19_out, out_21, out_19, out_20);
  and and_20 (and_20_out, d_ff_9_qn, d_ff_8_qn, d_ff_7_qn, out_18);
  D_Flip_Flop d_ff_5 (.D(or_3_out), .clk(clock_2_out), .Q(out_18), .Qn(d_ff_5_qn), .reset(Reset));  // open: preset
  or or_3 (or_3_out, and_20_out, and_19_out);
  Clock clock_2 (.out(clock_2_out));
  D_Flip_Flop #(.trigger("falling")) d_ff_6 (
    .D(and_22_out), .clk(clock_2_out), .Q(d_ff_6_q));  // open: Qn, preset, reset
  or or_4 (or_4_out, and_7_out, and_4_out);
  or or_5 (or_5_out, and_8_out, and_4_out);
  or or_6 (or_6_out, and_9_out, and_16_out);
  or or_7 (or_7_out, and_16_out, and_10_out);
  or or_8 (or_8_out, and_11_out, and_17_out);
  or or_9 (or_9_out, and_17_out, and_12_out);
  or or_10 (or_10_out, and_13_out, and_18_out);
  or or_11 (or_11_out, and_18_out, and_14_out);
  and and_21 (and_21_out, out_20, out_21);
  xor xor_2 (xor_2_out, and_21_out, out_19);
  and and_22 (and_22_out, out_18, d_ff_7_qn, d_ff_8_qn, out_21);
  and and_23 (and_23_out, d_ff_5_qn, out_21, d_ff_8_qn);
  D_Flip_Flop d_ff_7 (.D(xor_2_out), .clk(clock_2_out), .Q(out_19), .Qn(d_ff_7_qn), .reset(Reset));  // open: preset
  and and_24 (and_24_out, out_20, d_ff_9_qn);
  or or_12 (or_12_out, and_23_out, and_24_out);
  D_Flip_Flop d_ff_8 (.D(or_12_out), .clk(clock_2_out), .Q(out_20), .Qn(d_ff_8_qn), .reset(Reset));  // open: preset
  J_K_Flip_Flop j_k_ff_1 (.J(or_4_out), .K(or_5_out), .clk(clock_1_out), .Q(out_9), .reset(in_7));  // open: Qn, preset
  J_K_Flip_Flop j_k_ff_2 (.J(or_6_out), .K(or_7_out), .clk(clock_1_out), .Q(out_10), .reset(in_7));  // open: Qn, preset
  J_K_Flip_Flop j_k_ff_3 (.J(or_8_out), .K(or_9_out), .clk(clock_1_out), .Q(out_11), .reset(in_7));  // open: Qn, preset
  J_K_Flip_Flop j_k_ff_4 (
    .J(or_10_out), .K(or_11_out), .clk(clock_1_out), .Q(out_12), .reset(in_7));  // open: Qn, preset
  D_Flip_Flop d_ff_9 (.D(d_ff_9_qn), .clk(clock_2_out), .Q(out_21), .Qn(d_ff_9_qn), .reset(Reset));  // open: preset
  and and_25 (out_13, out_12, out_11, out_10, out_9, and_4_out);

  // Notes on the sheet:
  //   #2 2-digit BCD Counter
  //   #1 4-bit Counter with parallel load
endmodule
