// Logisim project 130_velasco_fajardo_me.circ as structural Verilog: 1 circuit, main circuit main
module main (
  input  in_1,
  input  in_2,
  input  in_3,
  input  in_4,
  input  [1:0] AddIn,
  input  Enabler,
  input  RW,
  input  [1:0] in_8,
  input  in_9,
  input  in_10,
  output out_11,
  output out_12,
  output out_13,
  output out_14,
  output [3:0] out_15
);

  wire and_1_out, and_2_out, and_3_out, and_4_out, and_5_out, and_6_out, and_7_out, and_8_out, and_9_out,
       and_10_out, and_11_out, and_12_out, and_13_out, and_14_out, and_15_out, and_16_out, and_17_out,
       and_18_out, and_19_out, and_20_out, and_21_out, and_22_out, and_23_out, and_24_out, and_25_out,
       and_26_out, and_27_out, and_28_out, and_29_out, and_30_out, and_31_out, and_32_out, decoder_1_out0,
       decoder_1_out1, decoder_1_out2, decoder_1_out3, nor_1_out, nor_2_out, nor_3_out, nor_4_out, nor_5_out,
       nor_6_out, nor_7_out, nor_8_out, nor_9_out, nor_10_out, nor_11_out, nor_12_out, nor_13_out,
       nor_14_out, nor_15_out, nor_16_out, not_1_out, not_2_out, not_3_out, not_4_out, not_5_out, not_6_out,
       not_7_out, not_8_out, not_9_out, not_10_out, not_11_out, not_12_out, not_13_out, not_14_out,
       not_15_out, not_16_out, not_17_out, not_18_out, not_19_out, not_20_out, not_21_out, not_22_out,
       not_23_out, not_24_out, not_25_out, not_26_out, not_27_out, not_28_out, not_29_out, not_30_out,
       not_31_out, not_32_out, Q_2_out, Q_3_out, Q_4_out, Q_5_out, Q_6_out, Q_7_out, Q_8_out, Q_9_out,
       Q_10_out, Q_11_out, Q_12_out, Q_13_out, Q_14_out, Q_15_out, Q_16_out, Q_out, reset_2_out, reset_3_out,
       reset_4_out, reset_5_out, reset_6_out, reset_7_out, reset_8_out, reset_9_out, reset_10_out,
       reset_11_out, reset_12_out, reset_13_out, reset_14_out, reset_15_out, reset_16_out, reset_out;

  Decoder #(.select(2)) decoder_1 (
    .out0(decoder_1_out0), .out1(decoder_1_out1), .out2(decoder_1_out2), .out3(decoder_1_out3), .sel(AddIn),
    .en(Enabler));
  not not_1 (not_1_out, RW);
  not not_2 (not_2_out, in_1);
  not not_3 (not_3_out, RW);
  not not_4 (not_4_out, in_1);
  not not_5 (not_5_out, RW);
  not not_6 (not_6_out, in_1);
  not not_7 (not_7_out, RW);
  not not_8 (not_8_out, in_1);
  and and_1 (and_1_out, decoder_1_out0, in_1, not_1_out);
  and reset (reset_out, decoder_1_out0, not_2_out, ~RW);  // AND_Gate
  and and_2 (and_2_out, decoder_1_out1, in_1, not_3_out);
  and reset_2 (reset_2_out, decoder_1_out1, not_4_out, ~RW);  // AND_Gate
  and and_3 (and_3_out, decoder_1_out2, in_1, not_5_out);
  and reset_3 (reset_3_out, decoder_1_out2, not_6_out, ~RW);  // AND_Gate
  and and_4 (and_4_out, decoder_1_out3, in_1, not_7_out);
  and reset_4 (reset_4_out, decoder_1_out3, not_8_out, ~RW);  // AND_Gate
  nor nor_1 (nor_1_out, and_1_out, Q_out);
  and and_5 (and_5_out, decoder_1_out0, Q_out, RW);
  nor Q (Q_out, nor_1_out, reset_out);
  nor nor_2 (nor_2_out, and_2_out, Q_2_out);
  and and_6 (and_6_out, decoder_1_out1, Q_2_out, RW);
  nor Q_2 (Q_2_out, nor_2_out, reset_2_out);
  nor nor_3 (nor_3_out, and_3_out, Q_3_out);
  and and_7 (and_7_out, decoder_1_out2, Q_3_out, RW);
  nor Q_3 (Q_3_out, nor_3_out, reset_3_out);
  nor nor_4 (nor_4_out, and_4_out, Q_4_out);
  and and_8 (and_8_out, decoder_1_out3, Q_4_out, RW);
  nor Q_4 (Q_4_out, nor_4_out, reset_4_out);
  or or_1 (out_11, and_8_out, and_7_out, and_6_out, and_5_out);
  not not_9 (not_9_out, in_2);
  not not_10 (not_10_out, in_2);
  not not_11 (not_11_out, in_2);
  not not_12 (not_12_out, in_2);
  RAM #(.addrWidth(2), .dataWidth(4)) ram_1 (.addr(in_8), .we(in_9), .oe(in_10), .data(out_15));  // open: clk
  and and_9 (and_9_out, decoder_1_out0, in_2, not_13_out);
  not not_13 (not_13_out, RW);
  and reset_5 (reset_5_out, decoder_1_out0, not_9_out, ~RW);  // AND_Gate
  and and_10 (and_10_out, decoder_1_out1, in_2, not_14_out);
  not not_14 (not_14_out, RW);
  and reset_6 (reset_6_out, decoder_1_out1, not_10_out, ~RW);  // AND_Gate
  and and_11 (and_11_out, decoder_1_out2, in_2, not_15_out);
  not not_15 (not_15_out, RW);
  and reset_7 (reset_7_out, decoder_1_out2, not_11_out, ~RW);  // AND_Gate
  and and_12 (and_12_out, decoder_1_out3, in_2, not_16_out);
  not not_16 (not_16_out, RW);
  and reset_8 (reset_8_out, decoder_1_out3, not_12_out, ~RW);  // AND_Gate
  nor nor_5 (nor_5_out, and_9_out, Q_5_out);
  nor Q_5 (Q_5_out, nor_5_out, reset_5_out);
  nor nor_6 (nor_6_out, and_10_out, Q_6_out);
  nor Q_6 (Q_6_out, nor_6_out, reset_6_out);
  nor nor_7 (nor_7_out, and_11_out, Q_7_out);
  nor Q_7 (Q_7_out, nor_7_out, reset_7_out);
  nor nor_8 (nor_8_out, and_12_out, Q_8_out);
  nor Q_8 (Q_8_out, nor_8_out, reset_8_out);
  and and_13 (and_13_out, decoder_1_out0, Q_5_out, RW);
  and and_14 (and_14_out, decoder_1_out1, Q_6_out, RW);
  and and_15 (and_15_out, decoder_1_out2, Q_7_out, RW);
  and and_16 (and_16_out, decoder_1_out3, Q_8_out, RW);
  or or_2 (out_12, and_16_out, and_15_out, and_14_out, and_13_out);
  not not_17 (not_17_out, RW);
  not not_18 (not_18_out, in_3);
  not not_19 (not_19_out, RW);
  not not_20 (not_20_out, in_3);
  not not_21 (not_21_out, RW);
  not not_22 (not_22_out, in_3);
  not not_23 (not_23_out, RW);
  not not_24 (not_24_out, in_3);
  and and_17 (and_17_out, decoder_1_out0, in_3, not_17_out);
  and reset_9 (reset_9_out, decoder_1_out0, not_18_out, ~RW);  // AND_Gate
  and and_18 (and_18_out, decoder_1_out1, in_3, not_19_out);
  and reset_10 (reset_10_out, decoder_1_out1, not_20_out, ~RW);  // AND_Gate
  and and_19 (and_19_out, decoder_1_out2, in_3, not_21_out);
  and reset_11 (reset_11_out, decoder_1_out2, not_22_out, ~RW);  // AND_Gate
  and and_20 (and_20_out, decoder_1_out3, in_3, not_23_out);
  and reset_12 (reset_12_out, decoder_1_out3, not_24_out, ~RW);  // AND_Gate
  nor nor_9 (nor_9_out, and_17_out, Q_9_out);
  and and_21 (and_21_out, decoder_1_out0, Q_9_out, RW);
  nor Q_9 (Q_9_out, nor_9_out, reset_9_out);
  nor nor_10 (nor_10_out, and_18_out, Q_10_out);
  and and_22 (and_22_out, decoder_1_out1, Q_10_out, RW);
  nor Q_10 (Q_10_out, nor_10_out, reset_10_out);
  nor nor_11 (nor_11_out, and_19_out, Q_11_out);
  and and_23 (and_23_out, decoder_1_out2, Q_11_out, RW);
  nor Q_11 (Q_11_out, nor_11_out, reset_11_out);
  nor nor_12 (nor_12_out, and_20_out, Q_12_out);
  and and_24 (and_24_out, decoder_1_out3, Q_12_out, RW);
  nor Q_12 (Q_12_out, nor_12_out, reset_12_out);
  or or_3 (out_13, and_24_out, and_23_out, and_22_out, and_21_out);
  not not_25 (not_25_out, in_4);
  not not_26 (not_26_out, in_4);
  not not_27 (not_27_out, in_4);
  not not_28 (not_28_out, in_4);
  and and_25 (and_25_out, decoder_1_out0, in_4, not_29_out);
  not not_29 (not_29_out, RW);
  and reset_13 (reset_13_out, decoder_1_out0, not_25_out, ~RW);  // AND_Gate
  and and_26 (and_26_out, decoder_1_out1, in_4, not_30_out);
  not not_30 (not_30_out, RW);
  and reset_14 (reset_14_out, decoder_1_out1, not_26_out, ~RW);  // AND_Gate
  and and_27 (and_27_out, decoder_1_out2, in_4, not_31_out);
  not not_31 (not_31_out, RW);
  and reset_15 (reset_15_out, decoder_1_out2, not_27_out, ~RW);  // AND_Gate
  and and_28 (and_28_out, decoder_1_out3, in_4, not_32_out);
  not not_32 (not_32_out, RW);
  and reset_16 (reset_16_out, decoder_1_out3, not_28_out, ~RW);  // AND_Gate
  nor nor_13 (nor_13_out, and_25_out, Q_13_out);
  nor Q_13 (Q_13_out, nor_13_out, reset_13_out);
  nor nor_14 (nor_14_out, and_26_out, Q_14_out);
  nor Q_14 (Q_14_out, nor_14_out, reset_14_out);
  nor nor_15 (nor_15_out, and_27_out, Q_15_out);
  nor Q_15 (Q_15_out, nor_15_out, reset_15_out);
  nor nor_16 (nor_16_out, and_28_out, Q_16_out);
  nor Q_16 (Q_16_out, nor_16_out, reset_16_out);
  and and_29 (and_29_out, decoder_1_out0, Q_13_out, RW);
  and and_30 (and_30_out, decoder_1_out1, Q_14_out, RW);
  and and_31 (and_31_out, decoder_1_out2, Q_15_out, RW);
  and and_32 (and_32_out, decoder_1_out3, Q_16_out, RW);
  or or_4 (out_14, and_32_out, and_31_out, and_30_out, and_29_out);

  // Notes on the sheet:
  //   set
  //   set
  //   set
  //   set
  //   set
  //   set
  //   set
  //   set
  //   set
  //   set
  //   set
  //   set
  //   set
  //   set
  //   set
  //   set
endmodule
