// Logisim project 130_velasco_le02.circ as structural Verilog: 1 circuit, main circuit main
module main (
  input  a,
  input  b,
  input  c,
  input  d,
  input  e,
  input  v,
  input  w,
  input  x,
  input  y,
  input  z,
  input  d0,
  input  d1,
  input  d2,
  input  d3,
  input  d4,
  input  d5,
  input  d6,
  input  d7,
  input  d8,
  input  d9,
  input  d10,
  input  d11,
  input  d12,
  input  d13,
  input  d14,
  input  d15,
  input  enabler,
  output F,
  output a_2,
  output b_2,
  output c_2,
  output d_2,
  output e_2,
  output status,
  output w_2,
  output x_2,
  output y_2,
  output z_2
);

  wire and_1_out, and_2_out, and_3_out, or_2_out, or_3_out, or_4_out, or_5_out, or_6_out;

  xor xor_1 (b_2, v, w);
  and and_1 (and_1_out, ~b, d);  // AND_Gate
  and and_2 (and_2_out, b, c);
  and and_3 (and_3_out, ~c, d);  // AND_Gate
  xor xor_2 (c_2, b_2, x);
  xor xor_3 (d_2, c_2, y);
  or or_1 (F, and_1_out, and_2_out, and_3_out);
  xor xor_4 (e_2, d_2, z);
  or or_2 (or_2_out, d15, d14, d13, d12, d11, d10, d9, d8, d7, d6, d5, d4, d3, d2, d1, d0);
  or or_3 (or_3_out, d8, d9, d10, d11, d12, d13, d14, d15);
  or or_4 (or_4_out, d4, d5, d6, d7, d12, d13, d14, d15);
  or or_5 (or_5_out, d2, d3, d6, d7, d10, d11, d14, d15);
  or or_6 (or_6_out, d1, d3, d5, d7, d9, d11, d13, d15);
  and and_4 (status, enabler, or_2_out);
  and and_5 (w_2, enabler, or_3_out);
  and and_6 (y_2, enabler, or_5_out);
  and and_7 (x_2, enabler, or_4_out);
  and and_8 (z_2, enabler, or_6_out);

  assign a_2 = v;

  // Notes on the sheet:
  //   I.A.2
  //   I.B.1
  //   F = b'd + bc + c'd
  //   II.B.
  //   III.B.
  //   ab\cde
  //   000
  //   00
  //   0
  //   01
  //   0
  //   11
  //   x
  //   10
  //   0
  //   011
  //   001
  //   0
  //   1
  //   x
  //   0
  //   0
  //   x
  //   1
  //   x
  //   010
  //   110
  //   1
  //   1
  //   1
  //   1
  //   1
  //   1
  //   1
  //   1
  //   101
  //   111
  //   1
  //   0
  //   1
  //   1
  //   1
  //   1
  //   x
  //   1
  //   100
  //   0
  //   1
  //   1
  //   0
  //   Gimel Velasco
  //   21BB
endmodule
