// Logisim project 130_velasco_me06.circ as structural Verilog: 1 circuit, main circuit main
module main (
  input  x4,
  input  x3,
  input  x2,
  input  x1,
  input  y4,
  input  y3,
  input  y2,
  input  y1,
  input  C0,
  output C4___ignore,
  output C3,
  output C2,
  output C1,
  output S4,
  output S3,
  output S2,
  output S1
);

  wire and_1_out, and_2_out, and_3_out, and_4_out, G0_out, G1_out, G3_out, G4_out, P0_out, P1_out, P3_out,
       P4_out, xor_2_out, xor_3_out, xor_5_out, xor_8_out;

  and G4 (G4_out, x4, y4);
  xor P4 (P4_out, x4, y4);
  or or_1 (C4___ignore, G4_out, and_1_out);
  and and_1 (and_1_out, P4_out, C3);
  xor xor_1 (S4, x4, xor_2_out);
  xor xor_2 (xor_2_out, y4, C3);
  and G3 (G3_out, x3, y3);
  xor P3 (P3_out, x3, y3);
  or or_2 (C3, G3_out, and_2_out);
  and and_2 (and_2_out, P3_out, C2);
  xor xor_3 (xor_3_out, y3, C2);
  xor xor_4 (S3, x3, xor_3_out);
  and G1 (G1_out, x2, y2);
  or or_3 (C2, G1_out, and_3_out);
  xor P1 (P1_out, x2, y2);
  and and_3 (and_3_out, P1_out, C1);
  xor xor_5 (xor_5_out, y2, C1);
  xor xor_6 (S2, x2, xor_5_out);
  and G0 (G0_out, x1, y1);
  or or_4 (C1, G0_out, and_4_out);
  xor xor_7 (S1, x1, xor_8_out);
  xor P0 (P0_out, x1, y1);
  and and_4 (and_4_out, P0_out, C0);
  xor xor_8 (xor_8_out, y1, C0);

  // Notes on the sheet:
  //   Sum
endmodule
