// Logisim project bc.circ as structural Verilog: 1 circuit, main circuit main
module main (
  input  select,
  input  \input ,
  input  input_2,
  input  read_if_1,
  input  input_3,
  input  input_4,
  input  [1:0] in_7,
  input  in_8,
  input  in_9,
  input  in_10,
  output out,
  output out_2,
  output out_3,
  output out_4,
  output [1:0] out_15
);

  wire and_1_out, and_2_out, and_5_out, and_6_out, nor_1_out, nor_2_out, nor_3_out, nor_4_out, nor_5_out,
       nor_6_out, nor_7_out, nor_8_out, not_1_out, not_2_out, not_3_out, not_4_out, not_5_out, not_6_out,
       not_7_out, not_8_out, not_9_out, reset_2_out, reset_3_out, reset_4_out, reset_out;

  not not_1 (not_1_out, input_2);
  not not_2 (not_2_out, select);
  not not_3 (not_3_out, input_4);
  RAM #(.addrWidth(2), .dataWidth(2)) ram_1 (.addr(in_7), .we(in_8), .oe(in_9), .clk(in_10), .data(out_15));
  and and_1 (and_1_out, select, input_2, not_4_out);
  and reset (reset_out, select, not_1_out, not_4_out);
  not not_4 (not_4_out, read_if_1);
  and and_2 (and_2_out, not_2_out, input_4, not_5_out);
  and reset_2 (reset_2_out, not_2_out, not_3_out, not_5_out);
  not not_5 (not_5_out, read_if_1);
  nor nor_1 (nor_1_out, and_1_out, nor_2_out);
  nor nor_2 (nor_2_out, nor_1_out, reset_out);
  nor nor_3 (nor_3_out, and_2_out, nor_4_out);
  nor nor_4 (nor_4_out, nor_3_out, reset_2_out);
  and and_3 (out_2, select, nor_2_out, read_if_1);
  and and_4 (out_4, not_2_out, nor_4_out, read_if_1);
  not not_6 (not_6_out, \input );
  not not_7 (not_7_out, input_3);
  and and_5 (and_5_out, select, \input , not_8_out);
  and reset_3 (reset_3_out, select, not_6_out, not_8_out);
  not not_8 (not_8_out, read_if_1);
  and and_6 (and_6_out, not_2_out, input_3, not_9_out);
  and reset_4 (reset_4_out, not_2_out, not_7_out, not_9_out);
  not not_9 (not_9_out, read_if_1);
  nor nor_5 (nor_5_out, and_5_out, nor_6_out);
  nor nor_6 (nor_6_out, nor_5_out, reset_3_out);
  nor nor_7 (nor_7_out, and_6_out, nor_8_out);
  nor nor_8 (nor_8_out, nor_7_out, reset_4_out);
  and and_7 (out, select, nor_6_out, read_if_1);
  and and_8 (out_3, not_2_out, nor_8_out, read_if_1);

  // Notes on the sheet:
  //   set
  //   set
  //   select
  //   set
  //   set
endmodule
